// Logisim project 7segmentdisplays (2).circ as structural Verilog
module bcd (
  input  A15,
  input  A14,
  input  A13,
  input  A12,
  input  A11,
  input  A10,
  input  A9,
  input  A8,
  input  A7,
  input  A6,
  input  A5,
  input  A4,
  input  A3,
  input  A2,
  input  A1,
  input  A0,
  output [3:0] out_17,
  output [3:0] out_18,
  output [3:0] out_19,
  output [3:0] out_20,
  output [3:0] out_21
);

  wire doubledabble_1_s0, doubledabble_1_s1, doubledabble_1_s2, doubledabble_1_s3, doubledabble_2_s0,
       doubledabble_2_s1, doubledabble_2_s2, doubledabble_2_s3, doubledabble_3_s0, doubledabble_3_s1,
       doubledabble_3_s2, doubledabble_3_s3, doubledabble_4_s0, doubledabble_4_s1, doubledabble_4_s2,
       doubledabble_4_s3, doubledabble_5_s0, doubledabble_5_s1, doubledabble_5_s2, doubledabble_5_s3,
       doubledabble_6_s0, doubledabble_6_s1, doubledabble_6_s2, doubledabble_6_s3, doubledabble_7_s0,
       doubledabble_7_s1, doubledabble_7_s2, doubledabble_7_s3, doubledabble_8_s0, doubledabble_8_s1,
       doubledabble_8_s2, doubledabble_8_s3, doubledabble_9_s0, doubledabble_9_s1, doubledabble_9_s2,
       doubledabble_9_s3, doubledabble_10_s0, doubledabble_10_s1, doubledabble_10_s2, doubledabble_10_s3,
       doubledabble_11_s0, doubledabble_11_s1, doubledabble_11_s2, doubledabble_11_s3, doubledabble_12_s0,
       doubledabble_12_s1, doubledabble_12_s2, doubledabble_12_s3, doubledabble_13_s0, doubledabble_13_s1,
       doubledabble_13_s2, doubledabble_13_s3, doubledabble_14_s0, doubledabble_14_s1, doubledabble_14_s2,
       doubledabble_14_s3, doubledabble_15_s0, doubledabble_15_s1, doubledabble_15_s2, doubledabble_15_s3,
       doubledabble_16_s0, doubledabble_16_s1, doubledabble_16_s2, doubledabble_16_s3, doubledabble_17_s0,
       doubledabble_17_s1, doubledabble_17_s2, doubledabble_17_s3, doubledabble_18_s0, doubledabble_18_s1,
       doubledabble_18_s2, doubledabble_18_s3, doubledabble_19_s0, doubledabble_19_s1, doubledabble_19_s2,
       doubledabble_19_s3, doubledabble_20_s0, doubledabble_20_s1, doubledabble_20_s2, doubledabble_20_s3,
       doubledabble_21_s0, doubledabble_21_s1, doubledabble_21_s2, doubledabble_21_s3, doubledabble_22_s0,
       doubledabble_22_s1, doubledabble_22_s2, doubledabble_23_s0, doubledabble_23_s1, doubledabble_23_s2,
       doubledabble_23_s3, doubledabble_24_s0, doubledabble_24_s1, doubledabble_24_s2, doubledabble_24_s3,
       doubledabble_25_s0, doubledabble_25_s1, doubledabble_25_s2, doubledabble_25_s3, doubledabble_26_s0,
       doubledabble_26_s1, doubledabble_26_s2, doubledabble_27_s0, doubledabble_27_s1, doubledabble_27_s2,
       doubledabble_27_s3, doubledabble_28_s0, doubledabble_28_s1, doubledabble_28_s2, doubledabble_28_s3,
       doubledabble_29_s0, doubledabble_29_s1, doubledabble_29_s2, doubledabble_29_s3;

  doubledabble doubledabble_1 (
    .A3(1'b0), .A2(A15), .A1(A14), .A0(A13), .S3(doubledabble_1_s3), .S2(doubledabble_1_s2),
    .S1(doubledabble_1_s1), .S0(doubledabble_1_s0));
  doubledabble doubledabble_2 (
    .A3(doubledabble_1_s2), .A2(doubledabble_1_s1), .A1(doubledabble_1_s0), .A0(A12), .S3(doubledabble_2_s3),
    .S2(doubledabble_2_s2), .S1(doubledabble_2_s1), .S0(doubledabble_2_s0));
  doubledabble doubledabble_3 (
    .A3(doubledabble_2_s2), .A2(doubledabble_2_s1), .A1(doubledabble_2_s0), .A0(A11), .S3(doubledabble_3_s3),
    .S2(doubledabble_3_s2), .S1(doubledabble_3_s1), .S0(doubledabble_3_s0));
  doubledabble doubledabble_4 (
    .A3(1'b0), .A2(doubledabble_1_s3), .A1(doubledabble_2_s3), .A0(doubledabble_3_s3),
    .S3(doubledabble_4_s3), .S2(doubledabble_4_s2), .S1(doubledabble_4_s1), .S0(doubledabble_4_s0));
  doubledabble doubledabble_5 (
    .A3(doubledabble_3_s2), .A2(doubledabble_3_s1), .A1(doubledabble_3_s0), .A0(A10), .S3(doubledabble_5_s3),
    .S2(doubledabble_5_s2), .S1(doubledabble_5_s1), .S0(doubledabble_5_s0));
  doubledabble doubledabble_6 (
    .A3(doubledabble_4_s2), .A2(doubledabble_4_s1), .A1(doubledabble_4_s0), .A0(doubledabble_5_s3),
    .S3(doubledabble_6_s3), .S2(doubledabble_6_s2), .S1(doubledabble_6_s1), .S0(doubledabble_6_s0));
  doubledabble doubledabble_7 (
    .A3(doubledabble_5_s2), .A2(doubledabble_5_s1), .A1(doubledabble_5_s0), .A0(A9), .S3(doubledabble_7_s3),
    .S2(doubledabble_7_s2), .S1(doubledabble_7_s1), .S0(doubledabble_7_s0));
  doubledabble doubledabble_8 (
    .A3(doubledabble_6_s2), .A2(doubledabble_6_s1), .A1(doubledabble_6_s0), .A0(doubledabble_7_s3),
    .S3(doubledabble_8_s3), .S2(doubledabble_8_s2), .S1(doubledabble_8_s1), .S0(doubledabble_8_s0));
  doubledabble doubledabble_9 (
    .A3(doubledabble_7_s2), .A2(doubledabble_7_s1), .A1(doubledabble_7_s0), .A0(A8), .S3(doubledabble_9_s3),
    .S2(doubledabble_9_s2), .S1(doubledabble_9_s1), .S0(doubledabble_9_s0));
  doubledabble doubledabble_10 (
    .A3(1'b0), .A2(doubledabble_4_s3), .A1(doubledabble_6_s3), .A0(doubledabble_8_s3),
    .S3(doubledabble_10_s3), .S2(doubledabble_10_s2), .S1(doubledabble_10_s1), .S0(doubledabble_10_s0));
  doubledabble doubledabble_11 (
    .A3(doubledabble_8_s2), .A2(doubledabble_8_s1), .A1(doubledabble_8_s0), .A0(doubledabble_9_s3),
    .S3(doubledabble_11_s3), .S2(doubledabble_11_s2), .S1(doubledabble_11_s1), .S0(doubledabble_11_s0));
  doubledabble doubledabble_12 (
    .A3(doubledabble_9_s2), .A2(doubledabble_9_s1), .A1(doubledabble_9_s0), .A0(A7), .S3(doubledabble_12_s3),
    .S2(doubledabble_12_s2), .S1(doubledabble_12_s1), .S0(doubledabble_12_s0));
  doubledabble doubledabble_13 (
    .A3(doubledabble_10_s2), .A2(doubledabble_10_s1), .A1(doubledabble_10_s0), .A0(doubledabble_11_s3),
    .S3(doubledabble_13_s3), .S2(doubledabble_13_s2), .S1(doubledabble_13_s1), .S0(doubledabble_13_s0));
  doubledabble doubledabble_14 (
    .A3(doubledabble_11_s2), .A2(doubledabble_11_s1), .A1(doubledabble_11_s0), .A0(doubledabble_12_s3),
    .S3(doubledabble_14_s3), .S2(doubledabble_14_s2), .S1(doubledabble_14_s1), .S0(doubledabble_14_s0));
  doubledabble doubledabble_15 (
    .A3(doubledabble_12_s2), .A2(doubledabble_12_s1), .A1(doubledabble_12_s0), .A0(A6),
    .S3(doubledabble_15_s3), .S2(doubledabble_15_s2), .S1(doubledabble_15_s1), .S0(doubledabble_15_s0));
  doubledabble doubledabble_16 (
    .A3(doubledabble_13_s2), .A2(doubledabble_13_s1), .A1(doubledabble_13_s0), .A0(doubledabble_14_s3),
    .S3(doubledabble_16_s3), .S2(doubledabble_16_s2), .S1(doubledabble_16_s1), .S0(doubledabble_16_s0));
  doubledabble doubledabble_17 (
    .A3(doubledabble_14_s2), .A2(doubledabble_14_s1), .A1(doubledabble_14_s0), .A0(doubledabble_15_s3),
    .S3(doubledabble_17_s3), .S2(doubledabble_17_s2), .S1(doubledabble_17_s1), .S0(doubledabble_17_s0));
  doubledabble doubledabble_18 (
    .A3(doubledabble_15_s2), .A2(doubledabble_15_s1), .A1(doubledabble_15_s0), .A0(A5),
    .S3(doubledabble_18_s3), .S2(doubledabble_18_s2), .S1(doubledabble_18_s1), .S0(doubledabble_18_s0));
  doubledabble doubledabble_19 (
    .A3(doubledabble_16_s2), .A2(doubledabble_16_s1), .A1(doubledabble_16_s0), .A0(doubledabble_17_s3),
    .S3(doubledabble_19_s3), .S2(doubledabble_19_s2), .S1(doubledabble_19_s1), .S0(doubledabble_19_s0));
  doubledabble doubledabble_20 (
    .A3(doubledabble_17_s2), .A2(doubledabble_17_s1), .A1(doubledabble_17_s0), .A0(doubledabble_18_s3),
    .S3(doubledabble_20_s3), .S2(doubledabble_20_s2), .S1(doubledabble_20_s1), .S0(doubledabble_20_s0));
  doubledabble doubledabble_21 (
    .A3(doubledabble_18_s2), .A2(doubledabble_18_s1), .A1(doubledabble_18_s0), .A0(A4),
    .S3(doubledabble_21_s3), .S2(doubledabble_21_s2), .S1(doubledabble_21_s1), .S0(doubledabble_21_s0));
  doubledabble doubledabble_22 (
    .A3(doubledabble_10_s3), .A2(doubledabble_13_s3), .A1(doubledabble_16_s3), .A0(doubledabble_19_s3),
    .S3(out_17[2]), .S2(doubledabble_22_s2), .S1(doubledabble_22_s1), .S0(doubledabble_22_s0));
  doubledabble doubledabble_23 (
    .A3(doubledabble_19_s2), .A2(doubledabble_19_s1), .A1(doubledabble_19_s0), .A0(doubledabble_20_s3),
    .S3(doubledabble_23_s3), .S2(doubledabble_23_s2), .S1(doubledabble_23_s1), .S0(doubledabble_23_s0));
  doubledabble doubledabble_24 (
    .A3(doubledabble_20_s2), .A2(doubledabble_20_s1), .A1(doubledabble_20_s0), .A0(doubledabble_21_s3),
    .S3(doubledabble_24_s3), .S2(doubledabble_24_s2), .S1(doubledabble_24_s1), .S0(doubledabble_24_s0));
  doubledabble doubledabble_25 (
    .A3(doubledabble_21_s2), .A2(doubledabble_21_s1), .A1(doubledabble_21_s0), .A0(A3),
    .S3(doubledabble_25_s3), .S2(doubledabble_25_s2), .S1(doubledabble_25_s1), .S0(doubledabble_25_s0));
  doubledabble doubledabble_26 (
    .A3(doubledabble_22_s2), .A2(doubledabble_22_s1), .A1(doubledabble_22_s0), .A0(doubledabble_23_s3),
    .S3(out_17[1]), .S2(doubledabble_26_s2), .S1(doubledabble_26_s1), .S0(doubledabble_26_s0));
  doubledabble doubledabble_27 (
    .A3(doubledabble_23_s2), .A2(doubledabble_23_s1), .A1(doubledabble_23_s0), .A0(doubledabble_24_s3),
    .S3(doubledabble_27_s3), .S2(doubledabble_27_s2), .S1(doubledabble_27_s1), .S0(doubledabble_27_s0));
  doubledabble doubledabble_28 (
    .A3(doubledabble_24_s2), .A2(doubledabble_24_s1), .A1(doubledabble_24_s0), .A0(doubledabble_25_s3),
    .S3(doubledabble_28_s3), .S2(doubledabble_28_s2), .S1(doubledabble_28_s1), .S0(doubledabble_28_s0));
  doubledabble doubledabble_29 (
    .A3(doubledabble_25_s2), .A2(doubledabble_25_s1), .A1(doubledabble_25_s0), .A0(A2),
    .S3(doubledabble_29_s3), .S2(doubledabble_29_s2), .S1(doubledabble_29_s1), .S0(doubledabble_29_s0));
  doubledabble doubledabble_30 (
    .A3(doubledabble_26_s2), .A2(doubledabble_26_s1), .A1(doubledabble_26_s0), .A0(doubledabble_27_s3),
    .S3(out_17[0]), .S2(out_18[3]), .S1(out_18[2]), .S0(out_18[1]));
  doubledabble doubledabble_31 (
    .A3(doubledabble_27_s2), .A2(doubledabble_27_s1), .A1(doubledabble_27_s0), .A0(doubledabble_28_s3),
    .S3(out_18[0]), .S2(out_19[3]), .S1(out_19[2]), .S0(out_19[1]));
  doubledabble doubledabble_32 (
    .A3(doubledabble_28_s2), .A2(doubledabble_28_s1), .A1(doubledabble_28_s0), .A0(doubledabble_29_s3),
    .S3(out_19[0]), .S2(out_20[3]), .S1(out_20[2]), .S0(out_20[1]));
  doubledabble doubledabble_33 (
    .A3(doubledabble_29_s2), .A2(doubledabble_29_s1), .A1(doubledabble_29_s0), .A0(A1), .S3(out_20[0]),
    .S2(out_21[3]), .S1(out_21[2]), .S0(out_21[1]));

  assign out_17[3] = 1'b0;
  assign out_21[0] = A0;
endmodule

module display (
  input  in_1,
  input  [1:0] in_2,
  input  [13:0] in_3
);

  wire bcd_to_7_segment_decoder_2_p2;
  wire [3:0] bcd_1_out_17, bcd_1_out_18, bcd_1_out_19, bcd_1_out_20, bcd_1_out_21,
       bcd_to_7_segment_decoder_1_p1, bcd_to_7_segment_decoder_2_p1, bcd_to_7_segment_decoder_3_p1;

  bcd bcd_1 (
    .A13(in_3[13]), .A12(in_3[12]), .A11(in_3[11]), .A10(in_3[10]), .A9(in_3[9]), .A8(in_3[8]), .A7(in_3[7]),
    .A6(in_3[6]), .A5(in_3[5]), .A4(in_3[4]), .A3(in_3[3]), .A2(in_3[2]), .A1(in_3[1]), .A0(in_3[0]),
    .out_17(bcd_1_out_17), .out_18(bcd_1_out_18), .out_19(bcd_1_out_19), .out_20(bcd_1_out_20),
    .out_21(bcd_1_out_21));  // open: A15, A14
  _7_Segment_Display u_7_segment_display_1 (.g(in_1));  // open: f, a, b, e, d, c, dp
  _7_Segment_Display u_7_segment_display_2 ();  // open: g, f, a, b, e, d, c, dp
  // BCD_to_7_Segment_decoder bcd_to_7_segment_decoder_1: pin names not known; wires that end beside it: bcd_to_7_segment_decoder_1_p1
  Multiplexer #(.select(2), .width(4)) multiplexer_1 (
    .in0(bcd_1_out_19), .in1(bcd_1_out_18), .in2(bcd_1_out_17), .out(bcd_to_7_segment_decoder_1_p1),
    .sel(in_2));  // open: in3
  _7_Segment_Display u_7_segment_display_3 ();  // open: g, f, a, b, e, d, c, dp
  _7_Segment_Display u_7_segment_display_4 ();  // open: g, f, a, b, e, d, c, dp
  // BCD_to_7_Segment_decoder bcd_to_7_segment_decoder_2: pin names not known; wires that end beside it: bcd_to_7_segment_decoder_2_p1, bcd_to_7_segment_decoder_2_p2, bcd_to_7_segment_decoder_2_p2
  // BCD_to_7_Segment_decoder bcd_to_7_segment_decoder_3: pin names not known; wires that end beside it: bcd_to_7_segment_decoder_3_p1
  Multiplexer #(.select(2), .width(4)) multiplexer_2 (
    .in0(bcd_1_out_20), .in1(bcd_1_out_19), .in2(bcd_1_out_18), .out(bcd_to_7_segment_decoder_2_p1),
    .sel(in_2));  // open: in3
  Multiplexer #(.select(2), .width(4)) multiplexer_3 (
    .in0(bcd_1_out_21), .in1(bcd_1_out_20), .in2(bcd_1_out_19), .out(bcd_to_7_segment_decoder_3_p1),
    .sel(in_2));  // open: in3
endmodule

module doubledabble (
  input  A3,
  input  A2,
  input  A1,
  input  A0,
  output S3,
  output S2,
  output S1,
  output S0
);

  wire and_1_out, and_2_out, and_3_out, and_4_out, not_1_out, or_1_out, or_2_out, xor_3_out, xor_4_out;

  or or_1 (or_1_out, A1, A0);
  and and_1 (and_1_out, A2, or_1_out);
  or or_2 (or_2_out, A3, and_1_out);
  xor xor_1 (S0, or_2_out, A0);
  not not_1 (not_1_out, A1);
  and and_2 (and_2_out, or_2_out, S0);
  and and_3 (and_3_out, not_1_out, and_2_out);
  xor xor_2 (S1, A1, and_2_out);
  xor xor_3 (xor_3_out, or_2_out, and_3_out);
  buf xor_4 (xor_4_out, xor_3_out);  // XOR_Gate
  and and_4 (and_4_out, A2, xor_4_out);
  xor xor_5 (S2, A2, xor_4_out);
  xor xor_6 (S3, A3, and_4_out);
endmodule
