// Logisim project Display- 8 bit.circ as structural Verilog: 1 circuit, main circuit display
module display (
  input  [7:0] in_1
);

  wire bcd_to_7_segment_decoder_1_p1, bcd_to_7_segment_decoder_2_p1, bcd_to_7_segment_decoder_3_p1;
  wire [7:0] adder_1_out, multiplexer_1_out, not_1_out;

  _7_Segment_Display u_7_segment_display_1 (.g(in_1[7]));  // open: f, a, b, e, d, c, dp
  assign not_1_out = ~in_1;  // NOT_Gate not_1, 8 bits wide
  _7_Segment_Display u_7_segment_display_2 ();  // open: g, f, a, b, e, d, c, dp
  _7_Segment_Display u_7_segment_display_3 ();  // open: g, f, a, b, e, d, c, dp
  // BCD_to_7_Segment_decoder bcd_to_7_segment_decoder_1: pin names not known; wires that end beside it: bcd_to_7_segment_decoder_1_p1
  // BCD_to_7_Segment_decoder bcd_to_7_segment_decoder_2: pin names not known; wires that end beside it: bcd_to_7_segment_decoder_2_p1
  Multiplexer #(.width(8)) multiplexer_1 (.in0(in_1), .in1(adder_1_out), .out(multiplexer_1_out), .sel(in_1[7]));
  Adder adder_1 (.a(not_1_out), .b(8'h1), .out(adder_1_out));  // open: cin, cout
  _7_Segment_Display u_7_segment_display_4 ();  // open: g, f, a, b, e, d, c, dp
  // BCD_to_7_Segment_decoder bcd_to_7_segment_decoder_3: pin names not known; wires that end beside it: bcd_to_7_segment_decoder_3_p1
  // Binary_to_BCD_converter #(.binvalue(8)) binary_to_bcd_converter_1: pin names not known; wires that end beside it: multiplexer_1_out, bcd_to_7_segment_decoder_1_p1, bcd_to_7_segment_decoder_2_p1, bcd_to_7_segment_decoder_3_p1
endmodule
