// Logisim project Finalsevensegment.circ as structural Verilog: 3 circuits, main circuit bcd
module bcd (
  input  [15:0] in_1,
  output [3:0] out_2,
  output [3:0] out_3,
  output [3:0] out_4,
  output [3:0] out_5,
  output [3:0] out_6
);

  wire doubledabble_1_s0, doubledabble_1_s1, doubledabble_1_s2, doubledabble_1_s3, doubledabble_2_s0,
       doubledabble_2_s1, doubledabble_2_s2, doubledabble_2_s3, doubledabble_3_s0, doubledabble_3_s1,
       doubledabble_3_s2, doubledabble_3_s3, doubledabble_4_s0, doubledabble_4_s1, doubledabble_4_s2,
       doubledabble_4_s3, doubledabble_5_s0, doubledabble_5_s1, doubledabble_5_s2, doubledabble_5_s3,
       doubledabble_6_s0, doubledabble_6_s1, doubledabble_6_s2, doubledabble_6_s3, doubledabble_7_s0,
       doubledabble_7_s1, doubledabble_7_s2, doubledabble_7_s3, doubledabble_8_s0, doubledabble_8_s1,
       doubledabble_8_s2, doubledabble_8_s3, doubledabble_9_s0, doubledabble_9_s1, doubledabble_9_s2,
       doubledabble_9_s3, doubledabble_10_s0, doubledabble_10_s1, doubledabble_10_s2, doubledabble_10_s3,
       doubledabble_11_s0, doubledabble_11_s1, doubledabble_11_s2, doubledabble_11_s3, doubledabble_12_s0,
       doubledabble_12_s1, doubledabble_12_s2, doubledabble_12_s3, doubledabble_13_s0, doubledabble_13_s1,
       doubledabble_13_s2, doubledabble_13_s3, doubledabble_14_s0, doubledabble_14_s1, doubledabble_14_s2,
       doubledabble_14_s3, doubledabble_15_s0, doubledabble_15_s1, doubledabble_15_s2, doubledabble_15_s3,
       doubledabble_16_s0, doubledabble_16_s1, doubledabble_16_s2, doubledabble_16_s3, doubledabble_17_s0,
       doubledabble_17_s1, doubledabble_17_s2, doubledabble_17_s3, doubledabble_18_s0, doubledabble_18_s1,
       doubledabble_18_s2, doubledabble_18_s3, doubledabble_19_s0, doubledabble_19_s1, doubledabble_19_s2,
       doubledabble_19_s3, doubledabble_20_s0, doubledabble_20_s1, doubledabble_20_s2, doubledabble_20_s3,
       doubledabble_21_s0, doubledabble_21_s1, doubledabble_21_s2, doubledabble_21_s3, doubledabble_22_s0,
       doubledabble_22_s1, doubledabble_22_s2, doubledabble_23_s0, doubledabble_23_s1, doubledabble_23_s2,
       doubledabble_23_s3, doubledabble_24_s0, doubledabble_24_s1, doubledabble_24_s2, doubledabble_24_s3,
       doubledabble_25_s0, doubledabble_25_s1, doubledabble_25_s2, doubledabble_25_s3, doubledabble_26_s0,
       doubledabble_26_s1, doubledabble_26_s2, doubledabble_27_s0, doubledabble_27_s1, doubledabble_27_s2,
       doubledabble_27_s3, doubledabble_28_s0, doubledabble_28_s1, doubledabble_28_s2, doubledabble_28_s3,
       doubledabble_29_s0, doubledabble_29_s1, doubledabble_29_s2, doubledabble_29_s3;

  doubledabble doubledabble_1 (
    .A3(1'b0), .A2(in_1[15]), .A1(in_1[14]), .A0(in_1[13]), .S3(doubledabble_1_s3), .S2(doubledabble_1_s2),
    .S1(doubledabble_1_s1), .S0(doubledabble_1_s0));
  doubledabble doubledabble_2 (
    .A3(doubledabble_1_s2), .A2(doubledabble_1_s1), .A1(doubledabble_1_s0), .A0(in_1[12]),
    .S3(doubledabble_2_s3), .S2(doubledabble_2_s2), .S1(doubledabble_2_s1), .S0(doubledabble_2_s0));
  doubledabble doubledabble_3 (
    .A3(doubledabble_2_s2), .A2(doubledabble_2_s1), .A1(doubledabble_2_s0), .A0(in_1[11]),
    .S3(doubledabble_3_s3), .S2(doubledabble_3_s2), .S1(doubledabble_3_s1), .S0(doubledabble_3_s0));
  doubledabble doubledabble_4 (
    .A3(1'b0), .A2(doubledabble_1_s3), .A1(doubledabble_2_s3), .A0(doubledabble_3_s3),
    .S3(doubledabble_4_s3), .S2(doubledabble_4_s2), .S1(doubledabble_4_s1), .S0(doubledabble_4_s0));
  doubledabble doubledabble_5 (
    .A3(doubledabble_3_s2), .A2(doubledabble_3_s1), .A1(doubledabble_3_s0), .A0(in_1[10]),
    .S3(doubledabble_5_s3), .S2(doubledabble_5_s2), .S1(doubledabble_5_s1), .S0(doubledabble_5_s0));
  doubledabble doubledabble_6 (
    .A3(doubledabble_4_s2), .A2(doubledabble_4_s1), .A1(doubledabble_4_s0), .A0(doubledabble_5_s3),
    .S3(doubledabble_6_s3), .S2(doubledabble_6_s2), .S1(doubledabble_6_s1), .S0(doubledabble_6_s0));
  doubledabble doubledabble_7 (
    .A3(doubledabble_5_s2), .A2(doubledabble_5_s1), .A1(doubledabble_5_s0), .A0(in_1[9]),
    .S3(doubledabble_7_s3), .S2(doubledabble_7_s2), .S1(doubledabble_7_s1), .S0(doubledabble_7_s0));
  doubledabble doubledabble_8 (
    .A3(doubledabble_6_s2), .A2(doubledabble_6_s1), .A1(doubledabble_6_s0), .A0(doubledabble_7_s3),
    .S3(doubledabble_8_s3), .S2(doubledabble_8_s2), .S1(doubledabble_8_s1), .S0(doubledabble_8_s0));
  doubledabble doubledabble_9 (
    .A3(doubledabble_7_s2), .A2(doubledabble_7_s1), .A1(doubledabble_7_s0), .A0(in_1[8]),
    .S3(doubledabble_9_s3), .S2(doubledabble_9_s2), .S1(doubledabble_9_s1), .S0(doubledabble_9_s0));
  doubledabble doubledabble_10 (
    .A3(1'b0), .A2(doubledabble_4_s3), .A1(doubledabble_6_s3), .A0(doubledabble_8_s3),
    .S3(doubledabble_10_s3), .S2(doubledabble_10_s2), .S1(doubledabble_10_s1), .S0(doubledabble_10_s0));
  doubledabble doubledabble_11 (
    .A3(doubledabble_8_s2), .A2(doubledabble_8_s1), .A1(doubledabble_8_s0), .A0(doubledabble_9_s3),
    .S3(doubledabble_11_s3), .S2(doubledabble_11_s2), .S1(doubledabble_11_s1), .S0(doubledabble_11_s0));
  doubledabble doubledabble_12 (
    .A3(doubledabble_9_s2), .A2(doubledabble_9_s1), .A1(doubledabble_9_s0), .A0(in_1[7]),
    .S3(doubledabble_12_s3), .S2(doubledabble_12_s2), .S1(doubledabble_12_s1), .S0(doubledabble_12_s0));
  doubledabble doubledabble_13 (
    .A3(doubledabble_10_s2), .A2(doubledabble_10_s1), .A1(doubledabble_10_s0), .A0(doubledabble_11_s3),
    .S3(doubledabble_13_s3), .S2(doubledabble_13_s2), .S1(doubledabble_13_s1), .S0(doubledabble_13_s0));
  doubledabble doubledabble_14 (
    .A3(doubledabble_11_s2), .A2(doubledabble_11_s1), .A1(doubledabble_11_s0), .A0(doubledabble_12_s3),
    .S3(doubledabble_14_s3), .S2(doubledabble_14_s2), .S1(doubledabble_14_s1), .S0(doubledabble_14_s0));
  doubledabble doubledabble_15 (
    .A3(doubledabble_12_s2), .A2(doubledabble_12_s1), .A1(doubledabble_12_s0), .A0(in_1[6]),
    .S3(doubledabble_15_s3), .S2(doubledabble_15_s2), .S1(doubledabble_15_s1), .S0(doubledabble_15_s0));
  doubledabble doubledabble_16 (
    .A3(doubledabble_13_s2), .A2(doubledabble_13_s1), .A1(doubledabble_13_s0), .A0(doubledabble_14_s3),
    .S3(doubledabble_16_s3), .S2(doubledabble_16_s2), .S1(doubledabble_16_s1), .S0(doubledabble_16_s0));
  doubledabble doubledabble_17 (
    .A3(doubledabble_14_s2), .A2(doubledabble_14_s1), .A1(doubledabble_14_s0), .A0(doubledabble_15_s3),
    .S3(doubledabble_17_s3), .S2(doubledabble_17_s2), .S1(doubledabble_17_s1), .S0(doubledabble_17_s0));
  doubledabble doubledabble_18 (
    .A3(doubledabble_15_s2), .A2(doubledabble_15_s1), .A1(doubledabble_15_s0), .A0(in_1[5]),
    .S3(doubledabble_18_s3), .S2(doubledabble_18_s2), .S1(doubledabble_18_s1), .S0(doubledabble_18_s0));
  doubledabble doubledabble_19 (
    .A3(doubledabble_16_s2), .A2(doubledabble_16_s1), .A1(doubledabble_16_s0), .A0(doubledabble_17_s3),
    .S3(doubledabble_19_s3), .S2(doubledabble_19_s2), .S1(doubledabble_19_s1), .S0(doubledabble_19_s0));
  doubledabble doubledabble_20 (
    .A3(doubledabble_17_s2), .A2(doubledabble_17_s1), .A1(doubledabble_17_s0), .A0(doubledabble_18_s3),
    .S3(doubledabble_20_s3), .S2(doubledabble_20_s2), .S1(doubledabble_20_s1), .S0(doubledabble_20_s0));
  doubledabble doubledabble_21 (
    .A3(doubledabble_18_s2), .A2(doubledabble_18_s1), .A1(doubledabble_18_s0), .A0(in_1[4]),
    .S3(doubledabble_21_s3), .S2(doubledabble_21_s2), .S1(doubledabble_21_s1), .S0(doubledabble_21_s0));
  doubledabble doubledabble_22 (
    .A3(doubledabble_10_s3), .A2(doubledabble_13_s3), .A1(doubledabble_16_s3), .A0(doubledabble_19_s3),
    .S3(out_2[2]), .S2(doubledabble_22_s2), .S1(doubledabble_22_s1), .S0(doubledabble_22_s0));
  doubledabble doubledabble_23 (
    .A3(doubledabble_19_s2), .A2(doubledabble_19_s1), .A1(doubledabble_19_s0), .A0(doubledabble_20_s3),
    .S3(doubledabble_23_s3), .S2(doubledabble_23_s2), .S1(doubledabble_23_s1), .S0(doubledabble_23_s0));
  doubledabble doubledabble_24 (
    .A3(doubledabble_20_s2), .A2(doubledabble_20_s1), .A1(doubledabble_20_s0), .A0(doubledabble_21_s3),
    .S3(doubledabble_24_s3), .S2(doubledabble_24_s2), .S1(doubledabble_24_s1), .S0(doubledabble_24_s0));
  doubledabble doubledabble_25 (
    .A3(doubledabble_21_s2), .A2(doubledabble_21_s1), .A1(doubledabble_21_s0), .A0(in_1[3]),
    .S3(doubledabble_25_s3), .S2(doubledabble_25_s2), .S1(doubledabble_25_s1), .S0(doubledabble_25_s0));
  doubledabble doubledabble_26 (
    .A3(doubledabble_22_s2), .A2(doubledabble_22_s1), .A1(doubledabble_22_s0), .A0(doubledabble_23_s3),
    .S3(out_2[1]), .S2(doubledabble_26_s2), .S1(doubledabble_26_s1), .S0(doubledabble_26_s0));
  doubledabble doubledabble_27 (
    .A3(doubledabble_23_s2), .A2(doubledabble_23_s1), .A1(doubledabble_23_s0), .A0(doubledabble_24_s3),
    .S3(doubledabble_27_s3), .S2(doubledabble_27_s2), .S1(doubledabble_27_s1), .S0(doubledabble_27_s0));
  doubledabble doubledabble_28 (
    .A3(doubledabble_24_s2), .A2(doubledabble_24_s1), .A1(doubledabble_24_s0), .A0(doubledabble_25_s3),
    .S3(doubledabble_28_s3), .S2(doubledabble_28_s2), .S1(doubledabble_28_s1), .S0(doubledabble_28_s0));
  doubledabble doubledabble_29 (
    .A3(doubledabble_25_s2), .A2(doubledabble_25_s1), .A1(doubledabble_25_s0), .A0(in_1[2]),
    .S3(doubledabble_29_s3), .S2(doubledabble_29_s2), .S1(doubledabble_29_s1), .S0(doubledabble_29_s0));
  doubledabble doubledabble_30 (
    .A3(doubledabble_26_s2), .A2(doubledabble_26_s1), .A1(doubledabble_26_s0), .A0(doubledabble_27_s3),
    .S3(out_2[0]), .S2(out_3[3]), .S1(out_3[2]), .S0(out_3[1]));
  doubledabble doubledabble_31 (
    .A3(doubledabble_27_s2), .A2(doubledabble_27_s1), .A1(doubledabble_27_s0), .A0(doubledabble_28_s3),
    .S3(out_3[0]), .S2(out_4[3]), .S1(out_4[2]), .S0(out_4[1]));
  doubledabble doubledabble_32 (
    .A3(doubledabble_28_s2), .A2(doubledabble_28_s1), .A1(doubledabble_28_s0), .A0(doubledabble_29_s3),
    .S3(out_4[0]), .S2(out_5[3]), .S1(out_5[2]), .S0(out_5[1]));
  doubledabble doubledabble_33 (
    .A3(doubledabble_29_s2), .A2(doubledabble_29_s1), .A1(doubledabble_29_s0), .A0(in_1[1]), .S3(out_5[0]),
    .S2(out_6[3]), .S1(out_6[2]), .S0(out_6[1]));

  assign out_2[3] = 1'b0;
  assign out_6[0] = in_1[0];
endmodule

module display (
  input  [1:0] in_1,
  input  [15:0] in_2
);

  wire bcd_to_7_segment_decoder_2_p2;
  wire [3:0] bcd_1_out_2, bcd_1_out_3, bcd_1_out_4, bcd_1_out_5, bcd_1_out_6, bcd_to_7_segment_decoder_1_p1,
       bcd_to_7_segment_decoder_2_p1, bcd_to_7_segment_decoder_3_p1;
  wire [15:0] adder_1_out, multiplexer_1_out, not_1_out;

  Multiplexer #(.width(16)) multiplexer_1 (.in0(in_2), .in1(adder_1_out), .out(multiplexer_1_out), .sel(in_2[15]));
  assign not_1_out = ~in_2;  // NOT_Gate not_1, 16 bits wide
  bcd bcd_1 (
    .in_1(multiplexer_1_out), .out_2(bcd_1_out_2), .out_3(bcd_1_out_3), .out_4(bcd_1_out_4),
    .out_5(bcd_1_out_5), .out_6(bcd_1_out_6));
  Adder #(.width(16)) adder_1 (.a(not_1_out), .b(16'h1), .out(adder_1_out));  // open: cin, cout
  _7_Segment_Display u_7_segment_display_1 (.g(in_2[15]));  // open: f, a, b, e, d, c, dp
  _7_Segment_Display u_7_segment_display_2 ();  // open: g, f, a, b, e, d, c, dp
  // BCD_to_7_Segment_decoder bcd_to_7_segment_decoder_1: pin names not known; wires that end beside it: bcd_to_7_segment_decoder_1_p1
  Multiplexer #(.select(2), .width(4)) multiplexer_2 (
    .in0(bcd_1_out_4), .in1(bcd_1_out_3), .in2(bcd_1_out_2), .out(bcd_to_7_segment_decoder_1_p1), .sel(in_1));  // open: in3
  _7_Segment_Display u_7_segment_display_3 ();  // open: g, f, a, b, e, d, c, dp
  _7_Segment_Display u_7_segment_display_4 ();  // open: g, f, a, b, e, d, c, dp
  // BCD_to_7_Segment_decoder bcd_to_7_segment_decoder_2: pin names not known; wires that end beside it: bcd_to_7_segment_decoder_2_p1, bcd_to_7_segment_decoder_2_p2, bcd_to_7_segment_decoder_2_p2
  // BCD_to_7_Segment_decoder bcd_to_7_segment_decoder_3: pin names not known; wires that end beside it: bcd_to_7_segment_decoder_3_p1
  Multiplexer #(.select(2), .width(4)) multiplexer_3 (
    .in0(bcd_1_out_5), .in1(bcd_1_out_4), .in2(bcd_1_out_3), .out(bcd_to_7_segment_decoder_2_p1), .sel(in_1));  // open: in3
  Multiplexer #(.select(2), .width(4)) multiplexer_4 (
    .in0(bcd_1_out_6), .in1(bcd_1_out_5), .in2(bcd_1_out_4), .out(bcd_to_7_segment_decoder_3_p1), .sel(in_1));  // open: in3
endmodule

module doubledabble (
  input  A3,
  input  A2,
  input  A1,
  input  A0,
  output S3,
  output S2,
  output S1,
  output S0
);

  wire and_1_out, and_2_out, and_3_out, and_4_out, not_1_out, or_1_out, or_2_out, xor_3_out, xor_4_out;

  or or_1 (or_1_out, A1, A0);
  and and_1 (and_1_out, A2, or_1_out);
  or or_2 (or_2_out, A3, and_1_out);
  xor xor_1 (S0, or_2_out, A0);
  not not_1 (not_1_out, A1);
  and and_2 (and_2_out, or_2_out, S0);
  and and_3 (and_3_out, not_1_out, and_2_out);
  xor xor_2 (S1, A1, and_2_out);
  xor xor_3 (xor_3_out, or_2_out, and_3_out);
  buf xor_4 (xor_4_out, xor_3_out);  // XOR_Gate
  and and_4 (and_4_out, A2, xor_4_out);
  xor xor_5 (S2, A2, xor_4_out);
  xor xor_6 (S3, A3, and_4_out);
endmodule
