// Logisim project spm.circ as structural Verilog: 5 circuits, main circuit TCMP
module TCMP (
  input  A,
  input  clk,
  input  R,
  output S
);

  wire d_ff_2_q, or_1_out, xor_1_out;

  xor xor_1 (xor_1_out, A, d_ff_2_q);
  or or_1 (or_1_out, A, d_ff_2_q);
  D_Flip_Flop d_ff_1 (.D(xor_1_out), .clk(clk), .Q(S), .reset(R));  // open: Qn, preset
  D_Flip_Flop d_ff_2 (.D(or_1_out), .clk(clk), .Q(d_ff_2_q), .reset(R));  // open: Qn, preset
endmodule

module half_adder (
  input  a,
  input  b,
  output sum,
  output carry
);

  xor xor_1 (sum, a, b);
  and and_1 (carry, a, b);
endmodule

module CSADD (
  input  x,
  input  in_2,
  input  clk,
  input  in_4,
  output sum
);

  wire and_1_out, d_ff_2_q, half_adder_1_carry, half_adder_1_sum, xor_1_out, xor_2_out;

  and and_1 (and_1_out, x, half_adder_1_sum);
  D_Flip_Flop d_ff_1 (.D(xor_1_out), .clk(clk), .Q(sum), .reset(in_4));  // open: Qn, preset
  xor xor_1 (xor_1_out, x, half_adder_1_sum);
  half_adder half_adder_1 (.a(in_2), .b(d_ff_2_q), .sum(half_adder_1_sum), .carry(half_adder_1_carry));
  xor xor_2 (xor_2_out, and_1_out, half_adder_1_carry);
  D_Flip_Flop d_ff_2 (.D(xor_2_out), .clk(clk), .Q(d_ff_2_q), .reset(in_4));  // open: Qn, preset

  // Notes on the sheet:
  //   y
  //   rst
endmodule

module main (
  input  in_1,
  input  in_2,
  input  in_3,
  input  in_4,
  input  in_5,
  input  [3:0] in_6,
  input  RSET,
  output [7:0] out_8
);

  wire and_1_out, and_2_out, and_3_out, and_4_out, bcd_to_7_segment_decoder_1_p1,
       bcd_to_7_segment_decoder_2_p1, bcd_to_7_segment_decoder_3_p1, clock_1_out, clock_2_out, clock_3_out,
       comparator_1_eq, csadd_1_sum, csadd_2_sum, csadd_3_sum, shift_register_1_p10, tcmp_1_s;
  wire [3:0] counter_1_q;
  wire [7:0] adder_1_out, multiplexer_1_out, not_1_out;

  Clock clock_1 (.out(clock_1_out));
  Clock clock_2 (.out(clock_2_out));
  // Shift_Register #(.length(4)) shift_register_1: pin names not known; wires that end beside it: RSET, in_1, 1'b1, clock_1_out, in_6[3], in_6[3], in_6[2], in_6[1], in_6[0], shift_register_1_p10
  and and_1 (and_1_out, shift_register_1_p10, in_2);
  TCMP tcmp_1 (.A(and_1_out), .clk(clock_2_out), .R(RSET), .S(tcmp_1_s));
  and and_2 (and_2_out, shift_register_1_p10, in_3);
  CSADD csadd_1 (.x(and_2_out), .in_2(tcmp_1_s), .clk(clock_2_out), .in_4(RSET), .sum(csadd_1_sum));
  and and_3 (and_3_out, shift_register_1_p10, in_4);
  CSADD csadd_2 (.x(and_3_out), .in_2(csadd_1_sum), .clk(clock_2_out), .in_4(RSET), .sum(csadd_2_sum));
  and and_4 (and_4_out, shift_register_1_p10, in_5);
  Counter #(.max('hf), .width(4)) counter_1 (
    .clr(RSET), .up(1'b1), .clk(clock_3_out), .Q(counter_1_q));  // open: load, count, D, carry
  CSADD csadd_3 (.x(and_4_out), .in_2(csadd_2_sum), .clk(clock_2_out), .in_4(RSET), .sum(csadd_3_sum));
  Clock clock_3 (.out(clock_3_out));
  // Shift_Register #(.trigger("falling")) shift_register_2: pin names not known; wires that end beside it: RSET, 1'b0, 1'b1, clock_3_out, csadd_3_sum, out_8[7], out_8[6], out_8[5], out_8[4], out_8[3], out_8[2], out_8[1], out_8[0]
  Comparator #(.width(4)) comparator_1 (.a(counter_1_q), .b(4'b1010), .eq(comparator_1_eq));  // open: gt, lt
  LED led_1 (.in(comparator_1_eq));
  _7_Segment_Display u_7_segment_display_1 (.g(out_8[7]));  // open: f, a, b, e, d, c, dp
  assign not_1_out = ~out_8;  // NOT_Gate not_1, 8 bits wide
  _7_Segment_Display u_7_segment_display_2 ();  // open: g, f, a, b, e, d, c, dp
  // BCD_to_7_Segment_decoder bcd_to_7_segment_decoder_1: pin names not known; wires that end beside it: bcd_to_7_segment_decoder_1_p1
  Multiplexer #(.width(8)) multiplexer_1 (.in0(out_8), .in1(adder_1_out), .out(multiplexer_1_out), .sel(out_8[7]));
  Adder adder_1 (.a(not_1_out), .b(8'h1), .out(adder_1_out));  // open: cin, cout
  _7_Segment_Display u_7_segment_display_3 ();  // open: g, f, a, b, e, d, c, dp
  _7_Segment_Display u_7_segment_display_4 ();  // open: g, f, a, b, e, d, c, dp
  // BCD_to_7_Segment_decoder bcd_to_7_segment_decoder_2: pin names not known; wires that end beside it: bcd_to_7_segment_decoder_2_p1
  // BCD_to_7_Segment_decoder bcd_to_7_segment_decoder_3: pin names not known; wires that end beside it: bcd_to_7_segment_decoder_3_p1
  // Binary_to_BCD_converter #(.binvalue(8)) binary_to_bcd_converter_1: pin names not known; wires that end beside it: multiplexer_1_out, bcd_to_7_segment_decoder_1_p1, bcd_to_7_segment_decoder_2_p1, bcd_to_7_segment_decoder_3_p1

  // Notes on the sheet:
  //   CLK
  //   x[3]
  //   x[2]
  //   x[1]
  //   x[0]
  //   LED (end of multiplication)
endmodule

module display (
  input  [7:0] in_1
);

  wire bcd_to_7_segment_decoder_1_p1, bcd_to_7_segment_decoder_2_p1, bcd_to_7_segment_decoder_3_p1;
  wire [7:0] adder_1_out, multiplexer_1_out, not_1_out;

  _7_Segment_Display u_7_segment_display_1 (.g(in_1[7]));  // open: f, a, b, e, d, c, dp
  assign not_1_out = ~in_1;  // NOT_Gate not_1, 8 bits wide
  _7_Segment_Display u_7_segment_display_2 ();  // open: g, f, a, b, e, d, c, dp
  _7_Segment_Display u_7_segment_display_3 ();  // open: g, f, a, b, e, d, c, dp
  // BCD_to_7_Segment_decoder bcd_to_7_segment_decoder_1: pin names not known; wires that end beside it: bcd_to_7_segment_decoder_1_p1
  // BCD_to_7_Segment_decoder bcd_to_7_segment_decoder_2: pin names not known; wires that end beside it: bcd_to_7_segment_decoder_2_p1
  Multiplexer #(.width(8)) multiplexer_1 (.in0(in_1), .in1(adder_1_out), .out(multiplexer_1_out), .sel(in_1[7]));
  Adder adder_1 (.a(not_1_out), .b(8'h1), .out(adder_1_out));  // open: cin, cout
  _7_Segment_Display u_7_segment_display_4 ();  // open: g, f, a, b, e, d, c, dp
  // BCD_to_7_Segment_decoder bcd_to_7_segment_decoder_3: pin names not known; wires that end beside it: bcd_to_7_segment_decoder_3_p1
  // Binary_to_BCD_converter #(.binvalue(8)) binary_to_bcd_converter_1: pin names not known; wires that end beside it: multiplexer_1_out, bcd_to_7_segment_decoder_1_p1, bcd_to_7_segment_decoder_2_p1, bcd_to_7_segment_decoder_3_p1
endmodule
